# Fritzing sketch Smart Home System (saved by Fritzing 0.9.3b)
breadboards: 1

parts:
  part = MH-ET LIVE ESP32 DEVKIT 38 pins
  part_2 = Piezo Speaker
  part_3 = Water Level Sensor
  part_4 = MLX90614 [package=to-39]
  part_5 = KY-026 Flame Sensor Module [package="Breakout board"]
  Part1 = MQ-4
  J1 = Basic Servo
  LCD1 = LCD screen
  LCM1602_IIC1 = LCM1602 IIC [part_number="LCM1602 IIC" chip_label="LCM1602 IIC" package="DIP (Dual Inline) [THT]"]
  Matrix_keypad1 = KEYPAD 4x4

nets:
  N1: part.IO34, J1.pulse
  N2: part.IO33, Matrix_keypad1.row4
  N3: part.IO25, Matrix_keypad1.row3
  N4: part.IO26, Matrix_keypad1.row2
  N5: part.IO27, Matrix_keypad1.row1
  N6: part.IO14, Matrix_keypad1.col4
  N7: part.IO12, Matrix_keypad1.col3
  N8: part.GND#58, Matrix_keypad1.col2
  N9: part.IO13, Matrix_keypad1.col1
  VCC: part.5V, part_2.pin1, part_3.VCC, part_4.VDD, part_5.+, Part1.VCC, J1.vcc, LCM1602_IIC1.VCC
  GND: part.GND#64, part_3.GND, part_4.VSS, part_5.G, Part1.GND, J1.gnd, LCM1602_IIC1.GND
  N10: part.IO23, part_2.pin2
  N11: part.IO22, part_3.SIG
  N12: part.IO19, part_5.A0
  N13: part.IO18, Part1.DO
  N14: part.SD1, LCM1602_IIC1.SDA
  N15: part.SD0, LCM1602_IIC1.SCL
  VSS: LCD1.VSS, LCM1602_IIC1.VSS
  VDD: LCD1.VDD, LCM1602_IIC1.VDD
  N16: LCD1.V0, LCM1602_IIC1.V0
  N17: LCD1.RS, LCM1602_IIC1.RS
  N18: LCD1.R/W, LCM1602_IIC1.RW
  N19: LCD1.E, LCM1602_IIC1.E
  N20: LCD1.DB0, LCM1602_IIC1.D0
  N21: LCD1.DB1, LCM1602_IIC1.D1
  N22: LCD1.DB2, LCM1602_IIC1.D2
  N23: LCD1.DB3, LCM1602_IIC1.D3
  N24: LCD1.DB4, LCM1602_IIC1.D4
  N25: LCD1.DB5, LCM1602_IIC1.D5
  N26: LCD1.DB6, LCM1602_IIC1.D6
  N27: LCD1.DB7, LCM1602_IIC1.D7
  N28: LCD1.LED+, LCM1602_IIC1.A
  N29: LCD1.LED-, LCM1602_IIC1.K

custom parts:
  MH-ET LIVE ESP32 DEVKIT 38 pins: http://mh.nodebb.com/topic/2/mh-et-live-esp32-devkit
  Water Level Sensor: A water level sensor. This sensor operates at 3V to 5V. The Sig (signal) pin outputs an analogue signal that is in proportion to the amount of water in contact with the sensor.
  KY-026 Flame Sensor Module: KY-026 Flame Sensor Module reacts in the presence of fire.
  LCM1602 IIC: I2C-Module to use a 1602 or 2004 LCD on with the wire.h libory Serial LCD Modul
  KEYPAD 4x4: Matrix keypad 16 buttons, 4 rows x 4 columns
